# Fritzing sketch WS (saved by Fritzing 0.9.3b)
breadboards: 2

parts:
  Arduino_MEGA = Arduino Mega 2560 (Rev3)
  RTC1307 = Real Time Clock Module - DS1307 RTC Breakout Board
  Potentiometer = Rotary Potentiometer (Large) [maximum_resistance=100kΩ package=THT]
  Potentiometer_2 = Rotary Potentiometer (Large) [maximum_resistance=100kΩ package=THT]
  ESP8266 = ESP8266 WiFi Module [part_number=ESP8266]
  SD_card_module = MicroSD Card Module
  LCD_display = LCD screen
  BME280 = BME280 Breakout

nets:
  N1: Arduino_MEGA.D21/SCL, RTC1307.SCL
  N2: Arduino_MEGA.D20/SDA, RTC1307.SDA
  N3: Arduino_MEGA.D19/RX1, ESP8266.TXD
  N4: Arduino_MEGA.D18/TX1, ESP8266.RXD
  N5: Arduino_MEGA.D12_PWM, LCD_display.RS
  N6: Arduino_MEGA.D11_PWM, LCD_display.E
  N7: Arduino_MEGA.D10_PWM, LCD_display.DB4
  N8: Arduino_MEGA.D9_PWM, LCD_display.DB5
  N9: Arduino_MEGA.D8_PWM, LCD_display.DB6
  3V3: Arduino_MEGA.3V3, ESP8266.VCC, ESP8266.CH_PD
  5V: Arduino_MEGA.5V, RTC1307.5V, Potentiometer.leg1, Potentiometer_2.leg1, SD_card_module.VCC, LCD_display.VDD
  GND: Arduino_MEGA.GND, RTC1307.GND, RTC1307.SQW, Potentiometer.leg2, Potentiometer_2.leg2, ESP8266.GND, SD_card_module.GND, LCD_display.VSS, LCD_display.R/W, LCD_display.LED-, BME280.GND
  N10: Arduino_MEGA.D4_PWM, SD_card_module.CS
  N11: Arduino_MEGA.D7_PWM, LCD_display.DB7
  N12: Arduino_MEGA.D50, SD_card_module.MISO
  N13: Arduino_MEGA.D51, SD_card_module.MOSI
  N14: Arduino_MEGA.D52, SD_card_module.SCK
  N15: Potentiometer.wiper, LCD_display.V0
  N16: Potentiometer_2.wiper, LCD_display.LED+

notes:
  ESP8266
  TTL serial
  VCC->3,3V
  GND->GND
  CH_PD->3,3V
  TXD->RXD
  RXD->TXD
  RTC1307
  I2C
  VCC->5V
  GND->GND
  SDA->SDA
  SCL->SCL
  BME280
  I2C
  VCC->5V
  GND->GND
  SCL->SCL
  SDA->SDA
  Catalex SD card module
  SPI
  VCC->5V
  GND->GND
  MISO->PIN 50
  MOSI->PIN 51
  SCK->PIN 52
  CS->PIN 4
  20x4 LCD display
  VSS->GND
  VDD->5V
  V0->potentiometer
  RS->PIN 12
  R/W->GND
  E->PIN 11
  D4->PIN 10
  D5->PIN 9
  D6->PIN 8
  D7->PIN 7
  LED+->potentiometer
  LCD-->GND
  Potentiometer
  LEG1->GND
  WIPER->LED+
  LEG2->5V
  Potentiometer
  LEG1->GND
  WIPER->VO
  LEG2->5V

custom parts:
  ESP8266 WiFi Module: Generic WiFi Module based on the ESP8266 with onboard PCB antenna and UART communications
